# Fritzing sketch 8led (saved by Fritzing 0.9.9b)
circuit board: 5.64cm x 8.46667cm
breadboards: 2

parts:
  R1 = Resistor [tolerance=±5% resistance=220 power=0.25 package=THT]
  J1 = female pin header, 8 pins [form="♀ (female)"]
  LED2 = LED - 5mm [color="Red (633nm)" current=0.030 package="5 mm [THT]"]
  LED3 = LED - 5mm [color="Red (633nm)" current=0.030 package="5 mm [THT]"]
  LED4 = LED - 5mm [color="Red (633nm)" current=0.030 package="5 mm [THT]"]
  LED5 = LED - 5mm [color="Red (633nm)" current=0.030 package="5 mm [THT]"]
  LED6 = LED - 5mm [color="Red (633nm)" current=0.030 package="5 mm [THT]"]
  LED7 = LED - 5mm [color="Red (633nm)" current=0.030 package="5 mm [THT]"]
  LED8 = LED - 5mm [color="Red (633nm)" current=0.030 package="5 mm [THT]"]
  R2 = Resistor [tolerance=±5% resistance=220 power=0.25 package=THT]
  R3 = Resistor [tolerance=±5% resistance=220 power=0.25 package=THT]
  R4 = Resistor [tolerance=±5% resistance=220 power=0.25 package=THT]
  R5 = Resistor [tolerance=±5% resistance=220 power=0.25 package=THT]
  R6 = Resistor [tolerance=±5% resistance=220 power=0.25 package=THT]
  R7 = Resistor [tolerance=±5% resistance=220 power=0.25 package=THT]
  R8 = Resistor [tolerance=±5% resistance=220 power=0.25 package=THT]
  NANO = Arduino Nano (Rev3.0)
  LED1 = LED - 5mm [color="Red (633nm)" current=0.030 package="5 mm [THT]"]
  S1 = Pushbutton [package="[THT]"]
  J2 = female pin header, 4 pins [form="♀ (female)"]  # not connected

nets:
  N1: R1.Pin_0, J1.pin1
  N2: R1.Pin_1, LED1.anode
  N3: J1.pin2, R2.Pin_0
  N4: J1.pin3, R3.Pin_0
  N5: J1.pin4, R4.Pin_0
  N6: J1.pin5, R5.Pin_0
  N7: J1.pin6, R6.Pin_0
  N8: J1.pin7, R7.Pin_0
  N9: J1.pin8, R8.Pin_0
  N10: LED2.cathode, LED3.cathode, LED4.cathode, LED5.cathode, LED6.cathode, LED7.cathode, LED8.cathode, NANO.GND, LED1.cathode
  N11: LED2.anode, R2.Pin_1
  N12: LED3.anode, R3.Pin_1
  N13: LED4.anode, R4.Pin_1
  N14: LED5.anode, R5.Pin_1
  N15: LED6.anode, R6.Pin_1
  N16: LED7.anode, R7.Pin_1
  N17: LED8.anode, R8.Pin_1
  N18: S1.Pin_1, S1.Pin_2
  N19: S1.Pin_3, S1.Pin_4
